# Fritzing sketch MazeUnlockReceiverScheme (saved by Fritzing 0.9.3b)
breadboards: 1

parts:
  Součástka2 = 24 NeoPixel Ring [part_number=1586]
  Součástka4 = Arduino Nano (Rev3.0)
  Součástka5 = NRF24L01+ Breakout Board
  J1 = Piezo Speaker
  SW1 = DIP Switch 8 Position [package=dipswitch-08]
  RST_button1 = Pushbutton [package="[THT]"]

nets:
  N1: Součástka2.IN, Součástka4.A2
  VDD: Součástka2.VDD, Součástka4.5V, SW1.8
  GND: Součástka2.GND, Součástka4.RESET, Součástka4.GND, Součástka5.GND, J1.pin1, RST_button1.Pin_1, RST_button1.Pin_2
  N2: Součástka4.D3, J1.pin2
  N3: Součástka4.D4, SW1.13
  N4: Součástka4.D5, SW1.14
  N5: Součástka4.D6, SW1.15
  N6: Součástka4.D11/MOSI, Součástka5.MOSI
  N7: Součástka4.D12/MISO, Součástka5.MISO
  N8: Součástka4.A6, Součástka5.CE
  N9: Součástka4.A5, Součástka5.CS
  3V3: Součástka4.3V3, Součástka5.VCC
  N10: Součástka4.D13/SCK, Součástka5.SCK

custom parts:
  24 NeoPixel Ring: 24 ultra bright smart LED NeoPixels are arranged in a circle with 2.6" (66mm) outer diameter. The rings are 'chainable' - connect the output pin of one to the input pin of another. Use only one microcontroller pin to control as many as you can chain together! Each LED is addressable as the driver chip is inside the LED. Each one has ~18mA constant current drive so the color will be very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
